// Digital circuit Control Unit.dig as structural Verilog
module Control_Unit (
  input  Nin,
  input  Vin,
  input  Zin,
  input  Cin,
  input  [7:0] IRin,
  input  ClockIn,
  input  RESET,
  output HALT,
  output MEM_LD_XDATA,
  output MEM_OUT_XDATA,
  output IR_LD_XDATA,
  output MBR_LD_XDATA,
  output MBR_OUT_XDATA,
  output MBR_LD_CDATA,
  output MBR_OUT_CDATA,
  output MARL_LD_CADDRL,
  output MARH_LD_CADDRH,
  output CDATA_TO_ADDRL,
  output CDATA_TO_ADDRH,
  output PC_INC,
  output PC_LD_ADD,
  output PC_OUT_CADDR,
  output PCL_LD_CADDRL,
  output PCH_LD_CADDRH,
  output STASH_LD_CDATA,
  output STASH_OUT_CDATA,
  output A_LD_CDATA,
  output A_OUT_CDATA,
  output X_LDCDATA,
  output X_OUT_CDATA,
  output Y_LD_CDATA,
  output Y_OUT_CDATA,
  output PN_LD,
  output V_LD,
  output Z_LD,
  output PC_LD,
  output P_SRC_0,
  output P_SRC_1,
  output ALUA_LD_DATA,
  output ALU_B_LD_CDATA,
  output ALUP_LD_P,
  output ALUR_OUT_CDATA,
  output ALU_OP0,
  output ALU_OP_1,
  output ALU_OP_2
);

  wire and_1_out, and_2_out, and_3_out, and_4_out, or_1_out, or_2_out, uCJMP, uJMP, uJMPINV, uJMPOP, uJSR,
       uNJMP, uPCINC, uRTS, uVJMP, uZJMP, xor_1_out, xor_2_out, xor_3_out, xor_4_out;
  wire [1:0] NextMux;
  wire [15:0] add_1_s, CAR, CARstore, multiplexer_2_out, Next, uCode_4_d, uNextAddr;

  Seven_Seg_Hex seven_seg_hex_1 (.d(CAR[11:8]), .dp(1'b0));
  Seven_Seg_Hex seven_seg_hex_2 (.d(CAR[15:12]), .dp(1'b0));
  Seven_Seg_Hex seven_seg_hex_3 (.d(uNextAddr[11:8]), .dp(1'b0));
  Seven_Seg_Hex seven_seg_hex_4 (.d(uNextAddr[15:12]), .dp(1'b0));
  Seven_Seg_Hex seven_seg_hex_5 (.d(CAR[3:0]), .dp(1'b0));
  Seven_Seg_Hex seven_seg_hex_6 (.d(CAR[7:4]), .dp(1'b0));
  Seven_Seg_Hex seven_seg_hex_7 (.d(uNextAddr[3:0]), .dp(1'b0));
  Seven_Seg_Hex seven_seg_hex_8 (.d(uNextAddr[7:4]), .dp(1'b0));
  Seven_Seg_Hex seven_seg_hex_9 (.d(CARstore[15:12]), .dp(1'b0));
  Seven_Seg_Hex seven_seg_hex_10 (.d(Next[15:12]), .dp(1'b0));
  Seven_Seg_Hex seven_seg_hex_11 (.d(CARstore[7:4]), .dp(1'b0));
  Seven_Seg_Hex seven_seg_hex_12 (.d(CARstore[11:8]), .dp(1'b0));
  Seven_Seg_Hex seven_seg_hex_13 (.d(Next[7:4]), .dp(1'b0));
  Seven_Seg_Hex seven_seg_hex_14 (.d(Next[11:8]), .dp(1'b0));
  Seven_Seg_Hex seven_seg_hex_15 (.d(CARstore[3:0]), .dp(1'b0));
  Seven_Seg_Hex seven_seg_hex_16 (.d(Next[3:0]), .dp(1'b0));
  LED led_1 (.in(NextMux[1]));
  LED led_2 (.in(NextMux[0]));
  ROM #(.AddrBits(16), .Bits(16)) uCode0 (.A(CAR), .sel(1'b1), .D(uNextAddr));
  ROM #(.AddrBits(16), .Bits(16)) uCode1 (
    .A(CAR), .sel(1'b1),
    .D({MBR_OUT_XDATA, MBR_LD_XDATA, IR_LD_XDATA, MEM_OUT_XDATA, MEM_LD_XDATA, HALT, uJMPINV, uCJMP, uZJMP, uVJMP, uNJMP, uJMPOP, uRTS, uJSR, uJMP, uPCINC}));
  ROM #(.AddrBits(16), .Bits(16)) uCode2 (
    .A(CAR), .sel(1'b1),
    .D({X_LDCDATA, A_OUT_CDATA, A_LD_CDATA, STASH_OUT_CDATA, STASH_LD_CDATA, PCH_LD_CADDRH, PCL_LD_CADDRL, PC_OUT_CADDR, PC_LD_ADD, PC_INC, CDATA_TO_ADDRH, CDATA_TO_ADDRL, MARH_LD_CADDRH, MARL_LD_CADDRL, MBR_OUT_CDATA, MBR_LD_CDATA}));
  ROM #(.AddrBits(16), .Bits(16)) uCode_3 (
    .A(CAR), .sel(1'b1),
    .D({ALU_OP_2, ALU_OP_1, ALU_OP0, ALUR_OUT_CDATA, ALUP_LD_P, ALU_B_LD_CDATA, ALUA_LD_DATA, P_SRC_1, P_SRC_0, PC_LD, Z_LD, V_LD, PN_LD, Y_OUT_CDATA, Y_LD_CDATA, X_OUT_CDATA}));
  ROM #(.AddrBits(16), .Bits(16)) uCode_4 (.A(CAR), .sel(1'b1), .D(uCode_4_d));
  Register #(.Bits(16)) u_CAR (.D(Next), .C(ClockIn), .en(1'b1), .Q(CAR));
  Add #(.Bits(16)) add_1 (.a(CAR), .b(16'h1), .c_i(1'b0), .s(add_1_s));  // open: c_o
  Multiplexer #(.Bits(16)) multiplexer_1 (.sel(RESET), .in_0(multiplexer_2_out), .in_1({16{1'b0}}), .out(Next));
  Register #(.Bits(16)) CAR_RTS (.D(add_1_s), .C(ClockIn), .en(uJSR), .Q(CARstore));
  or or_1 (or_1_out, uJMP, uJSR);
  and and_1 (and_1_out, uZJMP, xor_1_out);
  or or_2 (or_2_out, or_1_out, and_1_out, and_2_out, and_3_out, and_4_out);
  and and_2 (and_2_out, uNJMP, xor_2_out);
  xor xor_1 (xor_1_out, Zin, uJMPINV);
  Multiplexer #(.Selector_Bits(2), .Bits(16)) multiplexer_2 (
    .sel(NextMux), .in_0(add_1_s), .in_1(CARstore), .in_2(uNextAddr), .in_3({4'b0001, IRin, 4'b0000}),
    .out(multiplexer_2_out));
  or or_3 (NextMux[1], or_2_out, uJMPOP);
  and and_3 (and_3_out, uVJMP, xor_3_out);
  xor xor_2 (xor_2_out, Nin, uJMPINV);
  or or_4 (NextMux[0], uJMPOP, uRTS);
  and and_4 (and_4_out, uCJMP, xor_4_out);
  xor xor_3 (xor_3_out, Vin, uJMPINV);
  xor xor_4 (xor_4_out, Cin, uJMPINV);

  // Other names for the same wires on the sheet: PV_LD = V_LD; PZ_LD = Z_LD; ALUA_LD_CDATA = ALUA_LD_DATA;
  //   ALUB_LD_CDATA = ALU_B_LD_CDATA; ALUOP_0 = ALU_OP0; ALUOP_1 = ALU_OP_1; ALUOP_2 = ALU_OP_2;
  //   CDATA_TO_CADDRL = CDATA_TO_ADDRL; CDATA_TO_CADDRH = CDATA_TO_ADDRH; X_LD_CDATA = X_LDCDATA; Clock = ClockIn

  // Notes on the sheet:
  //   IRin: default 169
  //   CAR
  //   uNextAddr
  //   CAR RTS
  //   Next
  //   NextMux
  //   contents of uCode0 (hex, n*v repeats v):
  //   6000000,18000000,6000000,30000000,c0000000
  //   contents of uCode1 (hex, n*v repeats v):
  //   6000000,18000000,6000000,30000000,c0000000
  //   contents of uCode2 (hex, n*v repeats v):
  //   6000000,18000000,6000000,30000000,c0000000
  //   contents of uCode_3 (hex, n*v repeats v):
  //   6000000,18000000,6000000,30000000,c0000000
  //   contents of uCode_4 (hex, n*v repeats v):
  //   6000000,18000000,6000000,30000000,c0000000
endmodule
